# Fritzing sketch Activity 11 Schematic (saved by Fritzing 0.9.3b)
breadboards: 1

parts:
  Part1 = Arduino Uno (Rev3)
  R1 = Resistor [tolerance=±5% resistance=10k package=THT]
  Toggle_Switch_(Direction_Control) = Toggle Switch [package=THT]
  DC_Power_Supply_(5V) = 4 x AAA Battery Mount
  DC_Motor = DC Motor
  Toggle_Switch_(Motor_Enable) = Toggle Switch [package=THT]
  IC1 = H-Bridge [package=THT]
  Potentiometer_(ADC) = Trimmer Potentiometer [maximum_resistance=10kΩ package=THT]
  R2 = Resistor [tolerance=±5% resistance=10k package=THT]

nets:
  N1: Part1.A0, Potentiometer_(ADC).wiper
  GND: Part1.GND, R1.Pin_1, DC_Power_Supply_(5V).-, IC1.GND1, IC1.GND2, IC1.GND3, IC1.GND4, Potentiometer_(ADC).leg1, R2.Pin_1
  N2: Part1.D5_PWM, IC1.2A
  N3: Part1.D6_PWM, IC1.1A
  N4: Part1.D7, Toggle_Switch_(Direction_Control).COM
  N5: Part1.5V, Toggle_Switch_(Direction_Control).L1, Toggle_Switch_(Motor_Enable).L1, IC1.VCC1, Potentiometer_(ADC).leg2
  N6: R1.Pin_0, Toggle_Switch_(Motor_Enable).L2
  N7: Toggle_Switch_(Direction_Control).L2, R2.Pin_0
  N8: DC_Power_Supply_(5V).+, IC1.VCC2
  N9: DC_Motor.pin_1, IC1.1Y
  N10: DC_Motor.pin_2, IC1.2Y
  N11: Toggle_Switch_(Motor_Enable).COM, IC1.1_2EN
